# Fritzing sketch Scematic (saved by Fritzing 0.9.4)

parts:
  MH-ET_LIVE_ESP32_DEVKIT1 = MH-ET LIVE ESP32 DEVKIT 38 pins
  Grove1 = Grove OLED 128x96
  S1 = Momentary Switch [package=tactile-pth]
  U1 = ADMP504 - Ultralow Noise Microphone with Bottom Port and Analog Output [part_number=ADMP504]
  R1 = Resistor [tolerance=±5% resistance=10k package="2010 [SMD]"]

nets:
  3V3: MH-ET_LIVE_ESP32_DEVKIT1.3V3, Grove1.VCC, S1.4, U1.+
  GND: MH-ET_LIVE_ESP32_DEVKIT1.GND, Grove1.GND, U1.G
  N1: MH-ET_LIVE_ESP32_DEVKIT1.IO22, Grove1.SCL
  N2: MH-ET_LIVE_ESP32_DEVKIT1.IO21, Grove1.SDA
  N3: MH-ET_LIVE_ESP32_DEVKIT1.IO4, U1.A0
  N4: MH-ET_LIVE_ESP32_DEVKIT1.IO15, R1.Pin_0
  N5: S1.1, R1.Pin_1

custom parts:
  MH-ET LIVE ESP32 DEVKIT 38 pins: http://mh.nodebb.com/topic/2/mh-et-live-esp32-devkit
